// Logisim project dual_issue.circ as structural Verilog: 12 circuits, main circuit main
module main (
  input  rst,
  input  clk
);

  wire alu_1_outputready, alu_1_overflow, alu_2_outputready, alu_2_overflow, alu_3_outputready,
       alu_3_overflow, branchBusy, issue_1_stall1, issue_1_stall2, jumpcompare_1_readyo,
       memorycontroller_1_outputready, memorycontroller_1_ramwe, memorycontroller_1_storebool, not_1_out,
       registerstats_1_writelastinsregbool, reservationstations_1_add1ready, reservationstations_1_add2ready,
       reservationstations_1_add3ready, reservationstations_1_jmpnready, reservationstations_1_ldstreadytorun;
  wire [1:0] issue_1_newins1rd, issue_1_newins2rd, registerstats_1_writeregbools;
  wire [2:0] alu_1_outr, alu_2_outr, alu_3_outr, branchRS, issue_1_newins1rs, issue_1_newins2rs,
       jumpcompare_1_rso, memorycontroller_1_outr, registerstats_1_lastinsrs;
  wire [3:0] registerstats_1_writeregrds;
  wire [4:0] pc_1_icacheaddr;
  wire [5:0] aluRSs, cdbmanager_1_rss, ldstRSs, reservationstations_1_jmpnaddr;
  wire [7:0] issue_1_regreadr, issue_1_regstatr, pc_1_ins1, pc_1_ins2;
  wire [11:0] registerstats_1_readsres;
  wire [15:0] alu_1_result, alu_2_result, alu_3_result, jumpcompare_1_data, memorycontroller_1_dataout,
       memorycontroller_1_ramaddr, memorycontroller_1_ramdata, ram_1_dout, ram_2_dout,
       registerbank_1_mostrecentval, registerstats_1_writelastinsregval, reservationstations_1_jmpnvalue;
  wire [31:0] adder_1_out, cdbmanager_1_datas, register_1_q, registerstats_1_writeregvals;
  wire [38:0] reservationstations_1_add1ins, reservationstations_1_add2ins, reservationstations_1_add3ins,
       reservationstations_1_ldstins;
  wire [44:0] issue_1_openrsins1, issue_1_openrsins2;
  wire [63:0] registerbank_1_readval;

  RAM #(.addrWidth(5), .dataWidth(16), .trigger("falling")) ram_1 (
    .addr(pc_1_icacheaddr), .oe(1'b1), .clk(clk), .dout(ram_1_dout));  // open: we, din
  RegisterStats registerstats_1 (
    .new1RS(issue_1_newins1rs), .new1Rd(issue_1_newins1rd), .new2RS(issue_1_newins2rs),
    .new2Rd(issue_1_newins2rd), .CDBRSs(cdbmanager_1_rss), .clk(clk), .rst(rst), .readsR(issue_1_regstatr),
    .CDBDatas(cdbmanager_1_datas), .lastInsRS(registerstats_1_lastinsrs),
    .writeLastInsRegBool(registerstats_1_writelastinsregbool), .readsRes(registerstats_1_readsres),
    .writeRegVals(registerstats_1_writeregvals), .writeLastInsRegVal(registerstats_1_writelastinsregval),
    .writeRegRds(registerstats_1_writeregrds), .writeRegBools(registerstats_1_writeregbools));
  PC pc_1 (
    .clk(clk), .rst(rst), .stall2(issue_1_stall2), .ICacheData(ram_1_dout), .stall1(issue_1_stall1),
    .CDBdatas(cdbmanager_1_datas), .jumpRS(branchRS), .CDBRSs(cdbmanager_1_rss),
    .ICacheAddr(pc_1_icacheaddr), .ins2(pc_1_ins2), .ins1(pc_1_ins1));
  RegisterBank registerbank_1 (
    .readR(issue_1_regreadr), .clk(clk), .rst(rst), .writeRegBools(registerstats_1_writeregbools),
    .writeRegRds(registerstats_1_writeregrds), .writeRegVals(registerstats_1_writeregvals),
    .mostRecentValIn(registerstats_1_writelastinsregval),
    .mostRecentBool(registerstats_1_writelastinsregbool), .mostRecentVal(registerbank_1_mostrecentval),
    .readVal(registerbank_1_readval));
  Issue issue_1 (
    .rst(rst), .recentRS(registerstats_1_lastinsrs), .recentVal(registerbank_1_mostrecentval),
    .jumpRS(branchRS), .clk(clk), .jumpBusy(branchBusy), .openALURS(aluRSs), .openLDSTRS(ldstRSs),
    .ICacheIns2(pc_1_ins2), .regReadRes(registerbank_1_readval), .regStatRS(registerstats_1_readsres),
    .ICacheIns1(pc_1_ins1), .openRSIns1(issue_1_openrsins1), .newIns1Rd(issue_1_newins1rd),
    .newIns1RS(issue_1_newins1rs), .stall1(issue_1_stall1), .openRSIns2(issue_1_openrsins2),
    .regReadR(issue_1_regreadr), .regStatR(issue_1_regstatr), .newIns2Rd(issue_1_newins2rd),
    .newIns2RS(issue_1_newins2rs), .stall2(issue_1_stall2));
  ReservationStations reservationstations_1 (
    .rst(rst), .clk(clk), .CDBRSs(cdbmanager_1_rss), .CDBDatas(cdbmanager_1_datas),
    .storeDone(memorycontroller_1_storebool), .memRSdone(memorycontroller_1_outr),
    .openRSIns1(issue_1_openrsins1), .openRSIns2(issue_1_openrsins2),
    .add3ready(reservationstations_1_add3ready), .add3ins(reservationstations_1_add3ins),
    .add2ready(reservationstations_1_add2ready), .add2ins(reservationstations_1_add2ins),
    .add1ready(reservationstations_1_add1ready), .add1ins(reservationstations_1_add1ins), .rOpen(aluRSs),
    .jumpR(branchRS), .jmpRFull(branchBusy), .jmpnReady(reservationstations_1_jmpnready),
    .jmpnValue(reservationstations_1_jmpnvalue), .jmpnAddr(reservationstations_1_jmpnaddr),
    .ldstIns(reservationstations_1_ldstins), .ldstReadytorun(reservationstations_1_ldstreadytorun),
    .ldstOpenR(ldstRSs));
  JumpCompare jumpcompare_1 (
    .RS(branchRS), .ready(reservationstations_1_jmpnready), .address(reservationstations_1_jmpnaddr),
    .negCond(reservationstations_1_jmpnvalue), .RSo(jumpcompare_1_rso), .readyO(jumpcompare_1_readyo),
    .data(jumpcompare_1_data));
  RAM #(.addrWidth(16), .dataWidth(16), .trigger("falling")) ram_2 (
    .addr(memorycontroller_1_ramaddr), .we(memorycontroller_1_ramwe), .oe(not_1_out), .clk(clk),
    .din(memorycontroller_1_ramdata), .dout(ram_2_dout));
  not not_1 (not_1_out, memorycontroller_1_ramwe);
  Register #(.width(32)) register_1 (.D(adder_1_out), .en(1'b1), .clk(clk), .Q(register_1_q), .clr(rst));
  ALU alu_1 (
    .readyToEx(reservationstations_1_add1ready), .clk(clk), .rst(rst), .ins(reservationstations_1_add1ins),
    .Overflow(alu_1_overflow), .outputReady(alu_1_outputready), .result(alu_1_result), .outR(alu_1_outr));
  ALU alu_2 (
    .readyToEx(reservationstations_1_add2ready), .clk(clk), .rst(rst), .ins(reservationstations_1_add2ins),
    .Overflow(alu_2_overflow), .outputReady(alu_2_outputready), .result(alu_2_result), .outR(alu_2_outr));
  LED led_1 (.in(alu_2_overflow));
  ALU alu_3 (
    .readyToEx(reservationstations_1_add3ready), .clk(clk), .rst(rst), .ins(reservationstations_1_add3ins),
    .Overflow(alu_3_overflow), .outputReady(alu_3_outputready), .result(alu_3_result), .outR(alu_3_outr));
  LED led_2 (.in(alu_3_overflow));
  MemoryController memorycontroller_1 (
    .readyToEx(reservationstations_1_ldstreadytorun), .clk(clk), .rst(rst),
    .ins(reservationstations_1_ldstins), .RAMresult(ram_2_dout), .outR(memorycontroller_1_outr),
    .RAMaddr(memorycontroller_1_ramaddr), .RAMdata(memorycontroller_1_ramdata),
    .dataout(memorycontroller_1_dataout), .storeBool(memorycontroller_1_storebool),
    .outputReady(memorycontroller_1_outputready), .RAMWE(memorycontroller_1_ramwe));
  Adder #(.width(32)) adder_1 (.a(32'h1), .b(register_1_q), .out(adder_1_out));  // open: cin, cout
  LED led_3 (.in(alu_1_overflow));
  CDBManager cdbmanager_1 (
    .branchData(jumpcompare_1_data), .ldstRS(memorycontroller_1_outr), .ldstData(memorycontroller_1_dataout),
    .alu1RS(alu_1_outr), .alu1data(alu_1_result), .alu2RS(alu_2_outr), .alu2data(alu_2_result),
    .alu3RS(alu_3_outr), .alu3data(alu_3_result), .branchRS(jumpcompare_1_rso),
    .branchReady(jumpcompare_1_readyo), .ldstDone(memorycontroller_1_outputready),
    .ldstStore(memorycontroller_1_storebool), .alu1done(alu_1_outputready), .alu2done(alu_2_outputready),
    .alu3done(alu_3_outputready), .RSs(cdbmanager_1_rss), .datas(cdbmanager_1_datas));

  // Notes on the sheet:
  //   endless fibonacci:
  //   0e5e 9ede cb12 b28b 12e2 1000
  //   Register Stats
  //   Instruction Memory
  //   Program Counter
  //   Issue
  //   Logic
  //   Registers
  //   Reservation
  //   Stations
  //   ALUs
  //   RAM
  //   Common
  //   Data Bus
endmodule

module ReservationStations (
  input  clk,
  input  rst,
  input  [44:0] openRSIns1,
  input  [44:0] openRSIns2,
  input  [5:0] CDBRSs,
  input  [31:0] CDBDatas,
  input  storeDone,
  input  [2:0] memRSdone,
  output [5:0] rOpen,
  output add1ready,
  output [38:0] add1ins,
  output add2ready,
  output [38:0] add2ins,
  output add3ready,
  output [38:0] add3ins,
  output [38:0] ldstIns,
  output [5:0] ldstOpenR,
  output ldstReadytorun,
  output [2:0] jumpR,
  output jmpRFull,
  output jmpnReady,
  output [15:0] jmpnValue,
  output [5:0] jmpnAddr
);

  wire and_1_out, and_2_out, and_3_out, and_4_out, and_5_out, and_6_out, and_7_out, and_8_out, and_9_out,
       and_10_out, and_11_out, and_12_out, and_13_out, and_14_out, and_15_out, comparator_1_eq,
       comparator_2_eq, comparator_3_eq, comparator_4_eq, comparator_5_eq, comparator_6_eq, comparator_7_eq,
       comparator_8_eq, comparator_9_eq, comparator_10_eq, comparator_11_eq, comparator_12_eq,
       comparator_13_eq, comparator_14_eq, comparator_15_eq, comparator_16_eq, comparator_17_eq,
       comparator_18_eq, comparator_19_eq, comparator_20_eq, comparator_21_eq, ldst3onwritetop, nor_1_out,
       nor_2_out, not_2_out, not_3_out, not_4_out, or_1_out, or_2_out, or_3_out, or_4_out, or_5_out,
       or_6_out, or_7_out, or_8_out, queuetracker_1_imclearing, queuetracker_1_stacktop,
       queuetracker_2_imclearing, queuetracker_2_stacktop, queuetracker_3_imclearing,
       queuetracker_4_imclearing, queuetracker_4_stacktop, queuetracker_5_imclearing,
       queuetracker_5_stacktop, queuetracker_6_imclearing, queuetracker_6_stacktop, singlers_1_busyo,
       singlers_2_busyo, singlers_3_busyo, singlers_5_busyo, singlers_5_ready, singlers_6_busyo,
       singlers_6_ready, singlers_7_busyo, singlers_7_ready;
  wire [2:0] multiplexer_2_out, multiplexer_3_out, multiplexer_4_out, multiplexer_5_out, multiplexer_6_out,
       multiplexer_12_out, multiplexer_13_out, multiplexer_14_out, multiplexer_15_out, multiplexer_16_out;
  wire [15:6] singlers_4_out_16;
  wire [38:0] multiplexer_9_out, multiplexer_10_out, singlers_5_opfullo, singlers_6_opfullo,
       singlers_7_opfullo;

  Comparator #(.mode("unsigned"), .width(3)) comparator_1 (
    .a(openRSIns1[44:42]), .b(3'b100), .eq(comparator_1_eq));  // open: gt, lt
  Comparator #(.mode("unsigned"), .width(3)) comparator_2 (
    .a(3'b100), .b(openRSIns2[44:42]), .eq(comparator_2_eq));  // open: gt, lt
  Comparator #(.mode("unsigned"), .width(3)) comparator_3 (
    .a(openRSIns1[44:42]), .b(3'b101), .eq(comparator_3_eq));  // open: gt, lt
  Comparator #(.mode("unsigned"), .width(3)) comparator_4 (
    .a(3'b101), .b(openRSIns2[44:42]), .eq(comparator_4_eq));  // open: gt, lt
  Comparator #(.mode("unsigned"), .width(3)) comparator_5 (
    .a(openRSIns1[44:42]), .b(3'b110), .eq(comparator_5_eq));  // open: gt, lt
  Comparator #(.mode("unsigned"), .width(3)) comparator_6 (
    .a(3'b110), .b(openRSIns2[44:42]), .eq(comparator_6_eq));  // open: gt, lt
  or or_1 (or_1_out, comparator_1_eq, comparator_2_eq);
  or or_2 (or_2_out, comparator_3_eq, comparator_4_eq);
  or or_3 (or_3_out, comparator_5_eq, comparator_6_eq);
  QueueTracker queuetracker_1 (
    .prevClearing(queuetracker_3_imclearing), .clearCond(or_1_out), .clk(clk), .rst(rst),
    .stackTop(queuetracker_1_stacktop), .imClearing(queuetracker_1_imclearing));
  QueueTracker queuetracker_2 (
    .prevClearing(queuetracker_1_imclearing), .clearCond(or_2_out), .clk(clk), .rst(rst),
    .stackTop(queuetracker_2_stacktop), .imClearing(queuetracker_2_imclearing));
  QueueTracker queuetracker_3 (
    .prevClearing(queuetracker_2_imclearing), .clearCond(or_3_out), .clk(clk), .rst(rst),
    .stackTop(ldst3onwritetop), .imClearing(queuetracker_3_imclearing));
  nor nor_1 (nor_1_out, queuetracker_1_stacktop, queuetracker_2_stacktop, ldst3onwritetop);
  or or_4 (or_4_out, queuetracker_1_stacktop, nor_1_out);
  SingleRS singlers_1 (
    .rDone(CDBRSs), .clk(clk), .rst(rst), .r(3'b001), .res(CDBDatas), .openRSIns1(openRSIns1),
    .openRSIns2(openRSIns2), .ready(add1ready), .busyo(singlers_1_busyo), .opFullo(add1ins));  // open: forceClear, Qjo, Qko, opo, Vjo, out_16
  SingleRS singlers_2 (
    .rDone(CDBRSs), .clk(clk), .rst(rst), .r(3'b010), .res(CDBDatas), .openRSIns1(openRSIns1),
    .openRSIns2(openRSIns2), .ready(add2ready), .busyo(singlers_2_busyo), .opFullo(add2ins));  // open: forceClear, Qjo, Qko, opo, Vjo, out_16
  SingleRS singlers_3 (
    .rDone(CDBRSs), .clk(clk), .rst(rst), .r(3'b011), .res(CDBDatas), .openRSIns1(openRSIns1),
    .openRSIns2(openRSIns2), .ready(add3ready), .busyo(singlers_3_busyo), .opFullo(add3ins));  // open: forceClear, Qjo, Qko, opo, Vjo, out_16
  Comparator #(.mode("unsigned"), .width(3)) comparator_7 (
    .a(CDBRSs[2:0]), .b(3'b100), .eq(comparator_7_eq));  // open: gt, lt
  Comparator #(.mode("unsigned"), .width(3)) comparator_8 (
    .a(CDBRSs[5:3]), .b(3'b100), .eq(comparator_8_eq));  // open: gt, lt
  Comparator #(.mode("unsigned"), .width(3)) comparator_9 (
    .a(3'b100), .b(memRSdone), .eq(comparator_9_eq));  // open: gt, lt
  and and_1 (and_1_out, comparator_9_eq, storeDone);
  Comparator #(.mode("unsigned"), .width(3)) comparator_10 (
    .a(CDBRSs[2:0]), .b(3'b101), .eq(comparator_10_eq));  // open: gt, lt
  Comparator #(.mode("unsigned"), .width(3)) comparator_11 (
    .a(CDBRSs[5:3]), .b(3'b101), .eq(comparator_11_eq));  // open: gt, lt
  Comparator #(.mode("unsigned"), .width(3)) comparator_12 (
    .a(3'b101), .b(memRSdone), .eq(comparator_12_eq));  // open: gt, lt
  and and_2 (and_2_out, comparator_12_eq, storeDone);
  Comparator #(.mode("unsigned"), .width(3)) comparator_13 (
    .a(CDBRSs[2:0]), .b(3'b110), .eq(comparator_13_eq));  // open: gt, lt
  Comparator #(.mode("unsigned"), .width(3)) comparator_14 (
    .a(CDBRSs[5:3]), .b(3'b110), .eq(comparator_14_eq));  // open: gt, lt
  Comparator #(.mode("unsigned"), .width(3)) comparator_15 (
    .a(3'b110), .b(memRSdone), .eq(comparator_15_eq));  // open: gt, lt
  and and_3 (and_3_out, comparator_15_eq, storeDone);
  Multiplexer #(.width(3)) multiplexer_1 (
    .in0(3'b001), .in1(multiplexer_2_out), .out(rOpen[2:0]), .sel(singlers_1_busyo));
  Multiplexer #(.width(3)) multiplexer_2 (
    .in0(3'b010), .in1(multiplexer_3_out), .out(multiplexer_2_out), .sel(singlers_2_busyo));
  Multiplexer #(.width(3)) multiplexer_3 (.in0(3'b011), .in1(3'b000), .out(multiplexer_3_out), .sel(singlers_3_busyo));
  or or_5 (or_5_out, comparator_7_eq, comparator_8_eq, and_1_out);
  or or_6 (or_6_out, comparator_10_eq, comparator_11_eq, and_2_out);
  or or_7 (or_7_out, comparator_13_eq, comparator_14_eq, and_3_out);
  QueueTracker queuetracker_4 (
    .prevClearing(queuetracker_6_imclearing), .clearCond(or_5_out), .clk(clk), .rst(rst),
    .stackTop(queuetracker_4_stacktop), .imClearing(queuetracker_4_imclearing));
  QueueTracker queuetracker_5 (
    .prevClearing(queuetracker_4_imclearing), .clearCond(or_6_out), .clk(clk), .rst(rst),
    .stackTop(queuetracker_5_stacktop), .imClearing(queuetracker_5_imclearing));
  QueueTracker queuetracker_6 (
    .prevClearing(queuetracker_5_imclearing), .clearCond(or_7_out), .clk(clk), .rst(rst),
    .stackTop(queuetracker_6_stacktop), .imClearing(queuetracker_6_imclearing));
  Multiplexer #(.width(3)) multiplexer_4 (.in0(3'b001), .in1(3'b000), .out(multiplexer_4_out), .sel(singlers_1_busyo));
  Multiplexer #(.width(3)) multiplexer_5 (
    .in0(3'b010), .in1(multiplexer_4_out), .out(multiplexer_5_out), .sel(singlers_2_busyo));
  Multiplexer #(.width(3)) multiplexer_6 (
    .in0(3'b011), .in1(multiplexer_5_out), .out(multiplexer_6_out), .sel(singlers_3_busyo));
  nor nor_2 (nor_2_out, queuetracker_4_stacktop, queuetracker_5_stacktop, queuetracker_6_stacktop);
  or or_8 (or_8_out, queuetracker_4_stacktop, nor_2_out);
  Comparator #(.width(3)) comparator_16 (.a(rOpen[2:0]), .b(multiplexer_6_out), .eq(comparator_16_eq));  // open: gt, lt
  Multiplexer #(.width(3)) multiplexer_7 (
    .in0(multiplexer_6_out), .in1(3'b000), .out(rOpen[5:3]), .sel(comparator_16_eq));
  Comparator #(.mode("unsigned"), .width(3)) comparator_17 (
    .a(3'b100), .b(memRSdone), .eq(comparator_17_eq));  // open: gt, lt
  Comparator #(.mode("unsigned"), .width(3)) comparator_18 (
    .a(3'b101), .b(memRSdone), .eq(comparator_18_eq));  // open: gt, lt
  Comparator #(.mode("unsigned"), .width(3)) comparator_19 (
    .a(3'b110), .b(memRSdone), .eq(comparator_19_eq));  // open: gt, lt
  and and_4 (and_4_out, comparator_17_eq, storeDone);
  and and_5 (and_5_out, comparator_18_eq, storeDone);
  and and_6 (and_6_out, comparator_19_eq, storeDone);
  SingleRS singlers_4 (
    .rDone(CDBRSs), .clk(clk), .rst(rst), .r(3'b111), .res(CDBDatas), .openRSIns1(openRSIns1),
    .openRSIns2(openRSIns2), .ready(jmpnReady), .busyo(jmpRFull), .Vjo(jmpnValue),
    .out_16({singlers_4_out_16, jmpnAddr}));  // open: forceClear, Qjo, Qko, opo, opFullo
  SingleRS singlers_5 (
    .rDone(CDBRSs), .forceClear(and_4_out), .clk(clk), .rst(rst), .r(3'b100), .res(CDBDatas),
    .openRSIns1(openRSIns1), .openRSIns2(openRSIns2), .ready(singlers_5_ready), .busyo(singlers_5_busyo),
    .opFullo(singlers_5_opfullo));  // open: Qjo, Qko, opo, Vjo, out_16
  SingleRS singlers_6 (
    .rDone(CDBRSs), .forceClear(and_5_out), .clk(clk), .rst(rst), .r(3'b101), .res(CDBDatas),
    .openRSIns1(openRSIns1), .openRSIns2(openRSIns2), .ready(singlers_6_ready), .busyo(singlers_6_busyo),
    .opFullo(singlers_6_opfullo));  // open: Qjo, Qko, opo, Vjo, out_16
  SingleRS singlers_7 (
    .rDone(CDBRSs), .forceClear(and_6_out), .clk(clk), .rst(rst), .r(3'b110), .res(CDBDatas),
    .openRSIns1(openRSIns1), .openRSIns2(openRSIns2), .ready(singlers_7_ready), .busyo(singlers_7_busyo),
    .opFullo(singlers_7_opfullo));  // open: Qjo, Qko, opo, Vjo, out_16
  and and_7 (and_7_out, singlers_5_ready, or_8_out);
  and and_8 (and_8_out, singlers_6_ready, queuetracker_5_stacktop);
  and and_9 (and_9_out, singlers_7_ready, queuetracker_6_stacktop);
  Multiplexer #(.width(39)) multiplexer_8 (
    .in0(multiplexer_9_out), .in1(singlers_5_opfullo), .out(ldstIns), .sel(and_7_out));
  Multiplexer #(.width(39)) multiplexer_9 (
    .in0(multiplexer_10_out), .in1(singlers_6_opfullo), .out(multiplexer_9_out), .sel(and_8_out));
  Multiplexer #(.width(39)) multiplexer_10 (
    .in0({39{1'b0}}), .in1(singlers_7_opfullo), .out(multiplexer_10_out), .sel(and_9_out));
  not not_1 (ldstReadytorun, comparator_20_eq);
  Comparator #(.mode("unsigned"), .width(39)) comparator_20 (
    .a(ldstIns), .b({39{1'b0}}), .eq(comparator_20_eq));  // open: gt, lt
  not not_2 (not_2_out, singlers_5_busyo);
  not not_3 (not_3_out, singlers_6_busyo);
  not not_4 (not_4_out, singlers_7_busyo);
  and and_10 (and_10_out, not_2_out, or_4_out);
  and and_11 (and_11_out, not_3_out, queuetracker_2_stacktop);
  and and_12 (and_12_out, not_4_out, ldst3onwritetop);
  Multiplexer #(.width(3)) multiplexer_11 (
    .in0(multiplexer_12_out), .in1(3'b100), .out(ldstOpenR[2:0]), .sel(and_10_out));
  Multiplexer #(.width(3)) multiplexer_12 (
    .in0(multiplexer_13_out), .in1(3'b101), .out(multiplexer_12_out), .sel(and_11_out));
  Multiplexer #(.width(3)) multiplexer_13 (.in0(3'b000), .in1(3'b110), .out(multiplexer_13_out), .sel(and_12_out));
  and and_13 (and_13_out, ldst3onwritetop, not_2_out);
  and and_14 (and_14_out, or_4_out, not_3_out);
  and and_15 (and_15_out, queuetracker_2_stacktop, not_4_out);
  Multiplexer #(.width(3)) multiplexer_14 (
    .in0(multiplexer_15_out), .in1(3'b100), .out(multiplexer_14_out), .sel(and_13_out));
  Multiplexer #(.width(3)) multiplexer_15 (
    .in0(multiplexer_16_out), .in1(3'b101), .out(multiplexer_15_out), .sel(and_14_out));
  Multiplexer #(.width(3)) multiplexer_16 (.in0(3'b000), .in1(3'b110), .out(multiplexer_16_out), .sel(and_15_out));
  Comparator #(.width(3)) comparator_21 (
    .a(ldstOpenR[2:0]), .b(multiplexer_14_out), .eq(comparator_21_eq));  // open: gt, lt
  Multiplexer #(.width(3)) multiplexer_17 (
    .in0(multiplexer_14_out), .in1(3'b000), .out(ldstOpenR[5:3]), .sel(comparator_21_eq));

  assign jumpR = 3'b111;

  // Other names for the same wires on the sheet: CDBRS1[2:0] = CDBRSs[2:0]; CDBRS2[2:0] = CDBRSs[5:3];
  //   openIns1[44:0] = openRSIns1; openRS1[2:0] = openRSIns1[44:42]; openIns2[44:0] = openRSIns2;
  //   openRS2[2:0] = openRSIns2[44:42]; storeRS[2:0] = memRSdone

  // Notes on the sheet:
  //   Start Instruction
  //   Finish instruction
  //   update any matching
  //   Qk/Qj and set !busy
  //   write these values
  //   into the corresponding
  //   station
  //   write these values
  //   into the corresponding
  //   station
  //   op
  //   Vj
  //   Vk
  //   Qj
  //   Qk
  //   op
  //   Vj
  //   Vk
  //   Qj
  //   Qk
  //   alu1
  //   alu2
  //   alu3
  //   vacant stack
  //   open station #1
  //   bubble up
  //   to run queue
  //   open station #2
  //   bubble down
  //   jmp
  //   ldst1
  //   ldst2
  //   ldst3
  //   run
  //   write
  //   run
  //   write
  //   run
  //   write
  //   jmpnValue should just be forced
  //   negative for normal jumps, always
  //   checks
  //   bubble run
  //   open station #1
  //   bubble open
  //   open station #2
  //   bubble next open
endmodule

module SingleRS (
  input  [44:0] openRSIns1,
  input  [44:0] openRSIns2,
  input  clk,
  input  rst,
  input  [2:0] r,
  input  forceClear,
  input  [31:0] res,
  input  [5:0] rDone,
  output ready,
  output busyo,
  output [3:0] opo,
  output [38:0] opFullo,
  output [2:0] Qjo,
  output [15:0] Vjo,
  output [2:0] Qko,
  output [15:0] out_16
);

  wire and_1_out, and_2_out, and_3_out, and_4_out, CDBwrite1, CDBwrite2, comparator_1_eq, comparator_2_eq,
       comparator_3_eq, comparator_5_eq, comparator_6_eq, comparator_7_eq, comparator_8_eq, comparator_9_eq,
       comparator_10_eq, comparator_11_eq, comparator_12_eq, not_3_out, openThis, or_1_out, or_2_out,
       or_3_out, or_4_out, or_5_out, or_8_out, or_9_out, QjFinished, QkFinished, register_4_q;
  wire [2:0] multiplexer_2_out, multiplexer_3_out, QjNew, QkNew, rNew;
  wire [3:0] opNew;
  wire [15:0] multiplexer_4_out, multiplexer_5_out, multiplexer_6_out, multiplexer_7_out, VjNew, VkNew;

  not not_1 (CDBwrite1, comparator_1_eq);
  Comparator #(.mode("unsigned"), .width(3)) comparator_1 (
    .a(rDone[2:0]), .b(3'b000), .eq(comparator_1_eq));  // open: gt, lt
  not not_2 (CDBwrite2, comparator_2_eq);
  Comparator #(.mode("unsigned"), .width(3)) comparator_2 (
    .a(rDone[5:3]), .b(3'b000), .eq(comparator_2_eq));  // open: gt, lt
  Comparator #(.mode("unsigned"), .width(3)) comparator_3 (
    .a(openRSIns2[44:42]), .b(r), .eq(comparator_3_eq));  // open: gt, lt
  Multiplexer #(.width(45)) multiplexer_1 (
    .in0(openRSIns1), .in1(openRSIns2), .out({rNew, QkNew, QjNew, VkNew, VjNew, opNew}), .sel(comparator_3_eq));
  Comparator #(.mode("unsigned"), .width(3)) comparator_4 (.a(rNew), .b(r), .eq(openThis));  // open: gt, lt
  Comparator #(.mode("unsigned"), .width(3)) comparator_5 (
    .a(rDone[2:0]), .b(r), .eq(comparator_5_eq));  // open: gt, lt
  Comparator #(.mode("unsigned"), .width(3)) comparator_6 (
    .a(rDone[5:3]), .b(r), .eq(comparator_6_eq));  // open: gt, lt
  or or_1 (or_1_out, QjFinished, openThis);
  or or_2 (or_2_out, QkFinished, openThis);
  or or_3 (or_3_out, forceClear, comparator_5_eq, comparator_6_eq);
  not not_3 (not_3_out, or_3_out);
  Multiplexer #(.width(3)) multiplexer_2 (.in0(QjNew), .in1(3'b000), .out(multiplexer_2_out), .sel(QjFinished));
  Multiplexer #(.width(3)) multiplexer_3 (.in0(QkNew), .in1(3'b000), .out(multiplexer_3_out), .sel(QkFinished));
  or or_4 (or_4_out, openThis, not_3_out);
  or or_5 (or_5_out, or_3_out, openThis);
  Register #(.width(4)) register_1 (.D(opNew), .en(openThis), .clk(clk), .Q(opFullo[3:0]), .clr(rst));
  Register #(.width(3)) register_2 (.D(multiplexer_2_out), .en(or_1_out), .clk(clk), .Q(Qjo), .clr(rst));
  Register #(.width(3)) register_3 (.D(multiplexer_3_out), .en(or_2_out), .clk(clk), .Q(Qko), .clr(rst));
  Register #(.width(1)) register_4 (.D(or_4_out), .en(or_5_out), .clk(clk), .Q(register_4_q), .clr(rst));
  Comparator #(.mode("unsigned"), .width(3)) comparator_7 (.a(Qjo), .b(3'b000), .eq(comparator_7_eq));  // open: gt, lt
  Comparator #(.mode("unsigned"), .width(3)) comparator_8 (.a(Qko), .b(3'b000), .eq(comparator_8_eq));  // open: gt, lt
  Comparator #(.mode("unsigned"), .width(3)) comparator_9 (
    .a(rDone[2:0]), .b(Qjo), .eq(comparator_9_eq));  // open: gt, lt
  Comparator #(.mode("unsigned"), .width(3)) comparator_10 (
    .a(rDone[5:3]), .b(Qjo), .eq(comparator_10_eq));  // open: gt, lt
  Comparator #(.mode("unsigned"), .width(3)) comparator_11 (
    .a(rDone[2:0]), .b(Qko), .eq(comparator_11_eq));  // open: gt, lt
  Comparator #(.mode("unsigned"), .width(3)) comparator_12 (
    .a(rDone[5:3]), .b(Qko), .eq(comparator_12_eq));  // open: gt, lt
  and and_1 (and_1_out, CDBwrite1, comparator_9_eq);
  and and_2 (and_2_out, CDBwrite2, comparator_10_eq);
  and and_3 (and_3_out, CDBwrite1, comparator_11_eq);
  and and_4 (and_4_out, CDBwrite2, comparator_12_eq);
  and and_5 (ready, comparator_7_eq, comparator_8_eq, register_4_q);
  and and_6 (busyo, not_3_out, register_4_q);
  or or_6 (QjFinished, and_1_out, and_2_out);
  or or_7 (QkFinished, and_3_out, and_4_out);
  or or_8 (or_8_out, QjFinished, openThis);
  or or_9 (or_9_out, QkFinished, openThis);
  Multiplexer #(.width(16)) multiplexer_4 (.in0(VjNew), .in1(res[15:0]), .out(multiplexer_4_out), .sel(QjFinished));
  Multiplexer #(.width(16)) multiplexer_5 (
    .in0(multiplexer_4_out), .in1(res[31:16]), .out(multiplexer_5_out), .sel(and_2_out));
  Register #(.width(16)) register_5 (.D(multiplexer_5_out), .en(or_8_out), .clk(clk), .Q(opFullo[19:4]), .clr(rst));
  Multiplexer #(.width(16)) multiplexer_6 (.in0(VkNew), .in1(res[15:0]), .out(multiplexer_6_out), .sel(QkFinished));
  Multiplexer #(.width(16)) multiplexer_7 (
    .in0(multiplexer_6_out), .in1(res[31:16]), .out(multiplexer_7_out), .sel(and_4_out));
  Register #(.width(16)) register_6 (.D(multiplexer_7_out), .en(or_9_out), .clk(clk), .Q(opFullo[35:20]), .clr(rst));

  assign opFullo[38:36] = r;
  assign opo = opFullo[3:0];
  assign out_16 = opFullo[35:20];
  assign Vjo = opFullo[19:4];

  // Other names for the same wires on the sheet: Vko[15:0] = opFullo[35:20]; thisRS[2:0] = r;
  //   CDBRS1[2:0] = rDone[2:0]; CDBRS2[2:0] = rDone[5:3]; CDBval1[15:0] = res[15:0]; CDBval2[15:0] = res[31:16]

  // Notes on the sheet:
  //   am I finishing?
  //   dependancy done?
  //   J
  //   dependancy done?
  //   K
  //   Qj
  //   Qk
  //   op
  //   busy
  //   dependancy done?
  //   dependancy done?
  //   Vj
  //   Vj
endmodule

module QueueTracker (
  input  prevClearing,
  input  clearCond,
  input  clk,
  input  rst,
  output stackTop,
  output imClearing
);

  wire and_1_out, not_1_out;

  not not_1 (not_1_out, clearCond);
  and and_1 (and_1_out, prevClearing, not_1_out);
  J_K_Flip_Flop j_k_ff_1 (.J(and_1_out), .K(clearCond), .clk(clk), .Q(stackTop), .reset(rst));  // open: Qn, preset

  assign imClearing = clearCond;
endmodule

module ALU (
  input  [38:0] ins,
  input  clk,
  input  rst,
  input  readyToEx,
  output [2:0] outR,
  output outputReady,
  output [15:0] result,
  output Overflow
);

  wire and_1_out, and_3_out, and_4_out, and_5_out, not_1_out, not_2_out, not_3_out, not_4_out, not_6_out,
       or_1_out, or_2_out, or_3_out, sub, xor_1_out, xor_2_out;
  wire [14:0] multiplexer_1_out;
  wire [15:0] adder_1_out, multiplexer_3_out, not_5_out;
  wire [15:15] multiplexer_1_out_2;

  not not_1 (not_1_out, ins[3]);
  not not_2 (not_2_out, ins[2]);
  not not_3 (not_3_out, ins[1]);
  not not_4 (not_4_out, ins[0]);
  and and_1 (and_1_out, not_4_out, ins[1], not_2_out, not_1_out);
  and and_2 (sub, ins[0], ins[1], not_2_out, not_1_out);
  and and_3 (and_3_out, ins[3], ins[2], ins[1], not_4_out);
  and and_4 (and_4_out, not_1_out, ins[2], ins[1], not_4_out);
  Multiplexer #(.width(16)) multiplexer_1 (
    .in0(ins[19:4]), .in1(not_5_out), .out({multiplexer_1_out_2[15], multiplexer_1_out}), .sel(sub));
  assign not_5_out = ~ins[19:4];  // NOT_Gate not_5, 16 bits wide
  or or_1 (or_1_out, and_3_out, and_4_out);
  or or_2 (or_2_out, and_1_out, sub);
  Adder #(.width(16)) adder_1 (
    .a(ins[35:20]), .b({multiplexer_1_out_2[15], multiplexer_1_out}), .out(adder_1_out), .cin(sub));  // open: cout
  xor xor_1 (xor_1_out, multiplexer_1_out_2[15], ins[35]);
  xor xor_2 (xor_2_out, adder_1_out[15], multiplexer_1_out_2[15]);
  not not_6 (not_6_out, xor_1_out);
  Register #(.width(1)) register_1 (.D(1'b1), .en(and_5_out), .clk(clk), .Q(Overflow), .clr(rst));
  and and_5 (and_5_out, or_2_out, xor_2_out, not_6_out);
  or or_3 (or_3_out, or_2_out, or_1_out);
  and and_6 (outputReady, readyToEx, or_3_out);
  Multiplexer #(.width(16)) multiplexer_2 (.in0(multiplexer_3_out), .in1(adder_1_out), .out(result), .sel(or_2_out));
  Multiplexer #(.width(16)) multiplexer_3 (.in0({16{1'b0}}), .in1(ins[19:4]), .out(multiplexer_3_out), .sel(or_1_out));

  assign outR = ins[38:36];

  // Other names for the same wires on the sheet: op[3:0] = ins[3:0]; Vj[15:0] = ins[19:4]; Vk[15:0] = ins[35:20];
  //   Rnum[2:0] = ins[38:36]

  // Notes on the sheet:
  //   add
  //   sub
  //   ldi
  //   mv
  //   adder
endmodule

module MemoryController (
  input  readyToEx,
  input  [38:0] ins,
  input  clk,
  input  rst,
  input  [15:0] RAMresult,
  output [2:0] outR,
  output [15:0] RAMaddr,
  output [15:0] RAMdata,
  output [15:0] dataout,
  output outputReady,
  output RAMWE,
  output storeBool
);

  wire and_1_out, not_1_out, not_2_out, not_3_out, not_4_out, or_1_out;

  not not_1 (not_1_out, ins[3]);
  not not_2 (not_2_out, ins[2]);
  not not_3 (not_3_out, ins[1]);
  not not_4 (not_4_out, ins[0]);
  and and_1 (and_1_out, ins[0], ins[1], ins[2], ins[3]);
  and and_2 (storeBool, ins[0], ins[1], not_2_out, ins[3]);
  or or_1 (or_1_out, and_1_out, storeBool);
  and and_3 (outputReady, readyToEx, or_1_out);
  and and_4 (RAMWE, readyToEx, storeBool);

  assign dataout = RAMresult;
  assign outR = ins[38:36];
  assign RAMaddr = ins[19:4];
  assign RAMdata = ins[35:20];

  // Other names for the same wires on the sheet: op[3:0] = ins[3:0]; Vj[15:0] = ins[19:4]; Vk[15:0] = ins[35:20];
  //   Rnum[2:0] = ins[38:36]; ready = readyToEx

  // Notes on the sheet:
  //   ld
  //   st
  //   not writing any data back
  //   stores dont need to go to CDB
endmodule

module RegisterStats (
  input  clk,
  input  rst,
  input  [5:0] CDBRSs,
  input  [7:0] readsR,
  input  [2:0] new1RS,
  input  [1:0] new1Rd,
  input  [2:0] new2RS,
  input  [1:0] new2Rd,
  input  [31:0] CDBDatas,
  output [11:0] readsRes,
  output [3:0] writeRegRds,
  output [1:0] writeRegBools,
  output [2:0] lastInsRS,
  output writeLastInsRegBool,
  output [31:0] writeRegVals,
  output [15:0] writeLastInsRegVal
);

  wire and_1_out, and_2_out, and_3_out, and_4_out, and_5_out, and_6_out, and_7_out, and_8_out, CDBwrite1,
       CDBwrite2, comparator_1_eq, comparator_2_eq, comparator_3_eq, comparator_4_eq, comparator_5_eq,
       comparator_6_eq, comparator_7_eq, comparator_8_eq, comparator_9_eq, comparator_10_eq,
       comparator_11_eq, comparator_12_eq, comparator_13_eq, comparator_14_eq, comparator_15_eq,
       comparator_16_eq, comparator_17_eq, comparator_18_eq, comparator_19_eq, comparator_20_eq,
       comparator_21_eq, comparator_22_eq, fin0_1, fin0_2, fin1_1, fin1_2, fin2_1, fin2_2, fin3_1, fin3_2,
       fin4_1, fin4_2, newIns1Bool, newIns2Bool, or_5_out, or_6_out, or_7_out, or_8_out, or_9_out, or_10_out,
       or_11_out, or_12_out, or_13_out, or_14_out, we0, we1, we2, we3;
  wire [1:0] priority_encoder_1_out, priority_encoder_2_out;
  wire [2:0] in0, in1, in2, in3, multiplexer_2_out, multiplexer_4_out, multiplexer_6_out, multiplexer_8_out,
       multiplexer_9_out, multiplexer_10_out, o0, o1, o2, o3, register_1_q, register_2_q, register_3_q,
       register_4_q, register_5_q;
  wire [15:0] multiplexer_22_out;

  Comparator #(.width(3)) comparator_1 (.a(CDBRSs[2:0]), .b(3'b000), .eq(comparator_1_eq));  // open: gt, lt
  Comparator #(.width(3)) comparator_2 (.a(CDBRSs[5:3]), .b(3'b000), .eq(comparator_2_eq));  // open: gt, lt
  not not_1 (newIns1Bool, comparator_3_eq);
  Comparator #(.width(3)) comparator_3 (.a(new1RS), .b(3'b000), .eq(comparator_3_eq));  // open: gt, lt
  not not_2 (newIns2Bool, comparator_4_eq);
  Comparator #(.width(3)) comparator_4 (.a(new2RS), .b(3'b000), .eq(comparator_4_eq));  // open: gt, lt
  not not_3 (CDBwrite1, comparator_1_eq);
  not not_4 (CDBwrite2, comparator_2_eq);
  Comparator #(.width(2)) comparator_5 (.a(new2Rd), .b(2'b00), .eq(comparator_5_eq));  // open: gt, lt
  Comparator #(.width(2)) comparator_6 (.a(new1Rd), .b(2'b00), .eq(comparator_6_eq));  // open: gt, lt
  Comparator #(.width(2)) comparator_7 (.a(new2Rd), .b(2'b01), .eq(comparator_7_eq));  // open: gt, lt
  Comparator #(.width(2)) comparator_8 (.a(new1Rd), .b(2'b01), .eq(comparator_8_eq));  // open: gt, lt
  Comparator #(.width(2)) comparator_9 (.a(new2Rd), .b(2'b10), .eq(comparator_9_eq));  // open: gt, lt
  Comparator #(.width(2)) comparator_10 (.a(new1Rd), .b(2'b10), .eq(comparator_10_eq));  // open: gt, lt
  Comparator #(.width(2)) comparator_11 (.a(new2Rd), .b(2'b11), .eq(comparator_11_eq));  // open: gt, lt
  Comparator #(.width(2)) comparator_12 (.a(new1Rd), .b(2'b11), .eq(comparator_12_eq));  // open: gt, lt
  Multiplexer #(.width(3)) multiplexer_1 (.in0(multiplexer_2_out), .in1(new2RS), .out(in0), .sel(and_1_out));
  and and_1 (and_1_out, comparator_5_eq, newIns2Bool);
  Multiplexer #(.width(3)) multiplexer_2 (.in0(3'b000), .in1(new1RS), .out(multiplexer_2_out), .sel(and_2_out));
  and and_2 (and_2_out, comparator_6_eq, newIns1Bool);
  Multiplexer #(.width(3)) multiplexer_3 (.in0(multiplexer_4_out), .in1(new2RS), .out(in1), .sel(and_3_out));
  and and_3 (and_3_out, comparator_7_eq, newIns2Bool);
  Multiplexer #(.width(3)) multiplexer_4 (.in0(3'b000), .in1(new1RS), .out(multiplexer_4_out), .sel(and_4_out));
  and and_4 (and_4_out, comparator_8_eq, newIns1Bool);
  Multiplexer #(.width(3)) multiplexer_5 (.in0(multiplexer_6_out), .in1(new2RS), .out(in2), .sel(and_5_out));
  and and_5 (and_5_out, comparator_9_eq, newIns2Bool);
  Multiplexer #(.width(3)) multiplexer_6 (.in0(3'b000), .in1(new1RS), .out(multiplexer_6_out), .sel(and_6_out));
  and and_6 (and_6_out, comparator_10_eq, newIns1Bool);
  Multiplexer #(.width(3)) multiplexer_7 (.in0(multiplexer_8_out), .in1(new2RS), .out(in3), .sel(and_7_out));
  and and_7 (and_7_out, comparator_11_eq, newIns2Bool);
  Multiplexer #(.width(3)) multiplexer_8 (.in0(3'b000), .in1(new1RS), .out(multiplexer_8_out), .sel(and_8_out));
  and and_8 (and_8_out, comparator_12_eq, newIns1Bool);
  Multiplexer #(.width(3)) multiplexer_9 (
    .in0(multiplexer_10_out), .in1(new2RS), .out(multiplexer_9_out), .sel(newIns2Bool));
  Multiplexer #(.width(3)) multiplexer_10 (.in0(3'b000), .in1(new1RS), .out(multiplexer_10_out), .sel(newIns1Bool));
  or or_1 (we0, and_1_out, and_2_out);
  or or_2 (we1, and_3_out, and_4_out);
  or or_3 (we2, and_5_out, and_6_out);
  or or_4 (we3, and_7_out, and_8_out);
  or or_5 (or_5_out, newIns2Bool, newIns1Bool);
  or or_6 (or_6_out, or_11_out, we0);
  or or_7 (or_7_out, or_12_out, we1);
  or or_8 (or_8_out, or_13_out, we2);
  or or_9 (or_9_out, or_14_out, we3);
  or or_10 (or_10_out, writeLastInsRegBool, or_5_out);
  Register #(.width(3)) register_1 (.D(in0), .en(or_6_out), .clk(clk), .Q(register_1_q), .clr(rst));
  Register #(.width(3)) register_2 (.D(in1), .en(or_7_out), .clk(clk), .Q(register_2_q), .clr(rst));
  Register #(.width(3)) register_3 (.D(in2), .en(or_8_out), .clk(clk), .Q(register_3_q), .clr(rst));
  Register #(.width(3)) register_4 (.D(in3), .en(or_9_out), .clk(clk), .Q(register_4_q), .clr(rst));
  Register #(.width(3)) register_5 (.D(multiplexer_9_out), .en(or_10_out), .clk(clk), .Q(register_5_q), .clr(rst));
  Comparator #(.width(3)) comparator_13 (.a(register_1_q), .b(CDBRSs[2:0]), .eq(comparator_13_eq));  // open: gt, lt
  Comparator #(.width(3)) comparator_14 (.a(register_1_q), .b(CDBRSs[5:3]), .eq(comparator_14_eq));  // open: gt, lt
  Comparator #(.width(3)) comparator_15 (.a(register_2_q), .b(CDBRSs[2:0]), .eq(comparator_15_eq));  // open: gt, lt
  Comparator #(.width(3)) comparator_16 (.a(register_2_q), .b(CDBRSs[5:3]), .eq(comparator_16_eq));  // open: gt, lt
  Comparator #(.width(3)) comparator_17 (.a(register_3_q), .b(CDBRSs[2:0]), .eq(comparator_17_eq));  // open: gt, lt
  Comparator #(.width(3)) comparator_18 (.a(register_3_q), .b(CDBRSs[5:3]), .eq(comparator_18_eq));  // open: gt, lt
  and and_9 (fin0_1, comparator_13_eq, CDBwrite1);
  and and_10 (fin0_2, comparator_14_eq, CDBwrite2);
  and and_11 (fin1_1, comparator_15_eq, CDBwrite1);
  and and_12 (fin1_2, comparator_16_eq, CDBwrite2);
  and and_13 (fin2_1, comparator_17_eq, CDBwrite1);
  and and_14 (fin2_2, comparator_18_eq, CDBwrite2);
  Comparator #(.width(3)) comparator_19 (.a(register_4_q), .b(CDBRSs[2:0]), .eq(comparator_19_eq));  // open: gt, lt
  Comparator #(.width(3)) comparator_20 (.a(register_4_q), .b(CDBRSs[5:3]), .eq(comparator_20_eq));  // open: gt, lt
  Comparator #(.width(3)) comparator_21 (.a(register_5_q), .b(CDBRSs[2:0]), .eq(comparator_21_eq));  // open: gt, lt
  Comparator #(.width(3)) comparator_22 (.a(register_5_q), .b(CDBRSs[5:3]), .eq(comparator_22_eq));  // open: gt, lt
  or or_11 (or_11_out, fin0_1, fin0_2);
  or or_12 (or_12_out, fin1_1, fin1_2);
  or or_13 (or_13_out, fin2_1, fin2_2);
  and and_15 (fin3_1, comparator_19_eq, CDBwrite1);
  and and_16 (fin3_2, comparator_20_eq, CDBwrite2);
  and and_17 (fin4_1, comparator_21_eq, CDBwrite1);
  and and_18 (fin4_2, comparator_22_eq, CDBwrite2);
  or or_14 (or_14_out, fin3_1, fin3_2);
  or or_15 (writeLastInsRegBool, fin4_1, fin4_2);
  Multiplexer #(.width(3)) multiplexer_11 (.in0(register_1_q), .in1(3'b000), .out(o0), .sel(or_11_out));
  Multiplexer #(.width(3)) multiplexer_12 (.in0(register_2_q), .in1(3'b000), .out(o1), .sel(or_12_out));
  Multiplexer #(.width(3)) multiplexer_13 (.in0(register_3_q), .in1(3'b000), .out(o2), .sel(or_13_out));
  Multiplexer #(.width(3)) multiplexer_14 (.in0(register_4_q), .in1(3'b000), .out(o3), .sel(or_14_out));
  Multiplexer #(.width(3)) multiplexer_15 (
    .in0(register_5_q), .in1(3'b000), .out(lastInsRS), .sel(writeLastInsRegBool));
  Multiplexer #(.select(2), .width(3)) multiplexer_16 (
    .in0(o0), .in1(o1), .in2(o2), .in3(o3), .out(readsRes[2:0]), .sel(readsR[1:0]));
  Multiplexer #(.select(2), .width(3)) multiplexer_17 (
    .in0(o0), .in1(o1), .in2(o2), .in3(o3), .out(readsRes[5:3]), .sel(readsR[3:2]));
  Multiplexer #(.select(2), .width(3)) multiplexer_18 (
    .in0(o0), .in1(o1), .in2(o2), .in3(o3), .out(readsRes[8:6]), .sel(readsR[5:4]));
  Multiplexer #(.select(2), .width(3)) multiplexer_19 (
    .in0(o0), .in1(o1), .in2(o2), .in3(o3), .out(readsRes[11:9]), .sel(readsR[7:6]));
  Priority_Encoder #(.select(2)) priority_encoder_1 (
    .in0(fin0_1), .in1(fin1_1), .in2(fin2_1), .in3(fin3_1), .out(priority_encoder_1_out),
    .gs(writeRegBools[0]));  // open: en_out, en_in
  Priority_Encoder #(.select(2)) priority_encoder_2 (
    .in0(fin0_2), .in1(fin1_2), .in2(fin2_2), .in3(fin3_2), .out(priority_encoder_2_out),
    .gs(writeRegBools[1]));  // open: en_out, en_in
  Multiplexer #(.width(2)) multiplexer_20 (
    .in0(2'b00), .in1(priority_encoder_1_out), .out(writeRegRds[1:0]), .sel(writeRegBools[0]));
  Multiplexer #(.width(2)) multiplexer_21 (
    .in0(2'b00), .in1(priority_encoder_2_out), .out(writeRegRds[3:2]), .sel(writeRegBools[1]));
  Multiplexer #(.width(16)) multiplexer_22 (
    .in0({16{1'b0}}), .in1(CDBDatas[15:0]), .out(multiplexer_22_out), .sel(fin4_1));
  Multiplexer #(.width(16)) multiplexer_23 (
    .in0(multiplexer_22_out), .in1(CDBDatas[31:16]), .out(writeLastInsRegVal), .sel(fin4_2));

  assign writeRegVals = CDBDatas;

  // Other names for the same wires on the sheet: CDBRS1[2:0] = CDBRSs[2:0]; CDBRS2[2:0] = CDBRSs[5:3];
  //   fin4 = writeLastInsRegBool; o4[2:0] = lastInsRS

  // Notes on the sheet:
  //   finish instruction
  //   start new instruction
  //   most recent RS
  //   for jmpn
  //   R0
  //   R1
  //   R2
  //   R3
  //   2 bits/port
  //   Read ports
  //   registers must forward if on write line
  //   3 bits/port
endmodule

module RegisterBank (
  input  clk,
  input  rst,
  input  [1:0] writeRegBools,
  input  [31:0] writeRegVals,
  input  [7:0] readR,
  input  [3:0] writeRegRds,
  input  [15:0] mostRecentValIn,
  input  mostRecentBool,
  output [63:0] readVal,
  output [15:0] mostRecentVal
);

  wire and_1_out, and_2_out, and_3_out, and_4_out, and_5_out, and_6_out, and_7_out, and_8_out,
       comparator_1_eq, comparator_2_eq, comparator_3_eq, comparator_4_eq, comparator_5_eq, comparator_6_eq,
       comparator_7_eq, comparator_8_eq, or_1_out, or_2_out, or_3_out, or_4_out;
  wire [15:0] multiplexer_2_out, multiplexer_4_out, multiplexer_6_out, multiplexer_8_out, o0, o1, o2, o3,
       register_1_q, register_2_q, register_3_q, register_4_q, register_5_q;

  Comparator #(.width(2)) comparator_1 (.a(writeRegRds[1:0]), .b(2'b00), .eq(comparator_1_eq));  // open: gt, lt
  Comparator #(.width(2)) comparator_2 (.a(2'b00), .b(writeRegRds[3:2]), .eq(comparator_2_eq));  // open: gt, lt
  Comparator #(.width(2)) comparator_3 (.a(writeRegRds[1:0]), .b(2'b01), .eq(comparator_3_eq));  // open: gt, lt
  Comparator #(.width(2)) comparator_4 (.a(2'b01), .b(writeRegRds[3:2]), .eq(comparator_4_eq));  // open: gt, lt
  Comparator #(.width(2)) comparator_5 (.a(writeRegRds[1:0]), .b(2'b10), .eq(comparator_5_eq));  // open: gt, lt
  Comparator #(.width(2)) comparator_6 (.a(2'b10), .b(writeRegRds[3:2]), .eq(comparator_6_eq));  // open: gt, lt
  Comparator #(.width(2)) comparator_7 (.a(writeRegRds[1:0]), .b(2'b11), .eq(comparator_7_eq));  // open: gt, lt
  Comparator #(.width(2)) comparator_8 (.a(2'b11), .b(writeRegRds[3:2]), .eq(comparator_8_eq));  // open: gt, lt
  and and_1 (and_1_out, writeRegBools[0], comparator_1_eq);
  and and_2 (and_2_out, comparator_2_eq, writeRegBools[1]);
  and and_3 (and_3_out, writeRegBools[0], comparator_3_eq);
  and and_4 (and_4_out, comparator_4_eq, writeRegBools[1]);
  and and_5 (and_5_out, writeRegBools[0], comparator_5_eq);
  and and_6 (and_6_out, comparator_6_eq, writeRegBools[1]);
  and and_7 (and_7_out, writeRegBools[0], comparator_7_eq);
  and and_8 (and_8_out, comparator_8_eq, writeRegBools[1]);
  or or_1 (or_1_out, and_1_out, and_2_out);
  or or_2 (or_2_out, and_3_out, and_4_out);
  or or_3 (or_3_out, and_5_out, and_6_out);
  or or_4 (or_4_out, and_7_out, and_8_out);
  Register #(.width(16)) register_1 (.D(mostRecentValIn), .en(mostRecentBool), .clk(clk), .Q(register_1_q), .clr(rst));
  Register #(.width(16)) register_2 (.D(o0), .en(or_1_out), .clk(clk), .Q(register_2_q), .clr(rst));
  Register #(.width(16)) register_3 (.D(o1), .en(or_2_out), .clk(clk), .Q(register_3_q), .clr(rst));
  Register #(.width(16)) register_4 (.D(o2), .en(or_3_out), .clk(clk), .Q(register_4_q), .clr(rst));
  Register #(.width(16)) register_5 (.D(o3), .en(or_4_out), .clk(clk), .Q(register_5_q), .clr(rst));
  Multiplexer #(.width(16)) multiplexer_1 (
    .in0(register_1_q), .in1(mostRecentValIn), .out(mostRecentVal), .sel(mostRecentBool));
  Multiplexer #(.width(16)) multiplexer_2 (
    .in0(register_2_q), .in1(writeRegVals[15:0]), .out(multiplexer_2_out), .sel(or_1_out));
  Multiplexer #(.width(16)) multiplexer_3 (
    .in0(multiplexer_2_out), .in1(writeRegVals[31:16]), .out(o0), .sel(and_2_out));
  Multiplexer #(.width(16)) multiplexer_4 (
    .in0(register_3_q), .in1(writeRegVals[15:0]), .out(multiplexer_4_out), .sel(or_2_out));
  Multiplexer #(.width(16)) multiplexer_5 (
    .in0(multiplexer_4_out), .in1(writeRegVals[31:16]), .out(o1), .sel(and_4_out));
  Multiplexer #(.width(16)) multiplexer_6 (
    .in0(register_4_q), .in1(writeRegVals[15:0]), .out(multiplexer_6_out), .sel(or_3_out));
  Multiplexer #(.width(16)) multiplexer_7 (
    .in0(multiplexer_6_out), .in1(writeRegVals[31:16]), .out(o2), .sel(and_6_out));
  Multiplexer #(.width(16)) multiplexer_8 (
    .in0(register_5_q), .in1(writeRegVals[15:0]), .out(multiplexer_8_out), .sel(or_4_out));
  Multiplexer #(.width(16)) multiplexer_9 (
    .in0(multiplexer_8_out), .in1(writeRegVals[31:16]), .out(o3), .sel(and_8_out));
  Multiplexer #(.select(2), .width(16)) multiplexer_10 (
    .in0(o0), .in1(o1), .in2(o2), .in3(o3), .out(readVal[15:0]), .sel(readR[1:0]));
  Multiplexer #(.select(2), .width(16)) multiplexer_11 (
    .in0(o0), .in1(o1), .in2(o2), .in3(o3), .out(readVal[31:16]), .sel(readR[3:2]));
  Multiplexer #(.select(2), .width(16)) multiplexer_12 (
    .in0(o0), .in1(o1), .in2(o2), .in3(o3), .out(readVal[47:32]), .sel(readR[5:4]));
  Multiplexer #(.select(2), .width(16)) multiplexer_13 (
    .in0(o0), .in1(o1), .in2(o2), .in3(o3), .out(readVal[63:48]), .sel(readR[7:6]));

  // Other names for the same wires on the sheet: writing1 = writeRegBools[0]; writing2 = writeRegBools[1];
  //   writeRd1[1:0] = writeRegRds[1:0]; writeRd2[1:0] = writeRegRds[3:2]; writeVal1[15:0] = writeRegVals[15:0];
  //   writeVal2[15:0] = writeRegVals[31:16]

  // Notes on the sheet:
  //   two write ports
  //   start new instruction
  //   registers must forward if on write line
  //   2 bits/port
  //   Read ports
  //   16 bits/port
endmodule

module Issue (
  input  clk,
  input  rst,
  input  [2:0] recentRS,
  input  [15:0] recentVal,
  input  jumpBusy,
  input  [2:0] jumpRS,
  input  [5:0] openALURS,
  input  [5:0] openLDSTRS,
  input  [7:0] ICacheIns1,
  input  [7:0] ICacheIns2,
  input  [11:0] regStatRS,
  input  [63:0] regReadRes,
  output [44:0] openRSIns1,
  output [44:0] openRSIns2,
  output [7:0] regReadR,
  output [7:0] regStatR,
  output [2:0] newIns1RS,
  output [2:0] newIns2RS,
  output [1:0] newIns1Rd,
  output stall1,
  output stall2,
  output [1:0] newIns2Rd
);

  wire add1, add2, aluIns1, aluIns2, and_12_out, and_13_out, and_14_out, and_15_out, and_16_out, and_17_out,
       and_18_out, and_31_out, and_32_out, and_33_out, and_34_out, and_35_out, and_36_out, and_37_out,
       and_38_out, and_39_out, and_40_out, and_41_out, and_42_out, and_43_out, branchIns1, branchIns2,
       comparator_2_eq, comparator_3_eq, comparator_4_eq, comparator_5_eq, comparator_6_eq, comparator_7_eq,
       comparator_8_eq, comparator_9_eq, comparator_10_eq, comparator_11_eq, halt1, halt2, jmp1, jmp2, jmpn1,
       jmpn2, ld1, ld2, ldi1, ldi2, ldstIns1, ldstIns2, mv1, mv2, needsRd1, needsRd2, needsRs1, needsRs2,
       nop1, nop2, nostations1, nostations2, not_5_out, not_6_out, not_7_out, not_8_out, not_9_out,
       not_10_out, not_11_out, not_12_out, not_13_out, not_14_out, not_15_out, not_16_out, not_17_out,
       not_18_out, not_19_out, not_20_out, not_21_out, not_22_out, not_23_out, not_24_out, not_25_out,
       not_26_out, not_27_out, not_28_out, not_29_out, not_30_out, not_31_out, not_32_out, not_33_out,
       not_34_out, not_35_out, not_36_out, not_37_out, not_38_out, not_39_out, not_40_out, not_41_out,
       not_42_out, openALUstations1, openALUstations2, openLDSTstations1, openLDSTstations2, or_1_out,
       or_8_out, or_9_out, or_10_out, or_11_out, or_13_out, or_15_out, or_16_out, or_17_out, or_22_out,
       or_23_out, or_24_out, recentReady, st1, st2, sub1, sub2, writesRd1, writesRd2;
  wire [2:0] multiplexer_7_out, multiplexer_10_out, multiplexer_11_out, multiplexer_12_out,
       multiplexer_17_out, multiplexer_22_out, multiplexer_25_out, multiplexer_26_out, multiplexer_28_out,
       multiplexer_29_out, multiplexer_30_out, multiplexer_31_out, multiplexer_32_out, newRS1, newRS2,
       QjOut1, QjOut2, QkOut1, QkOut2;
  wire [15:0] multiplexer_3_out, multiplexer_4_out, multiplexer_5_out, multiplexer_14_out,
       multiplexer_19_out, multiplexer_20_out, multiplexer_21_out, multiplexer_34_out, VjOut1, VjOut2,
       VkOut1, VkOut2;

  Comparator #(.width(3)) comparator_1 (.a(recentRS), .b(3'b000), .eq(recentReady));  // open: gt, lt
  Comparator #(.mode("unsigned"), .width(3)) comparator_2 (
    .a(openALURS[2:0]), .b(3'b000), .eq(comparator_2_eq));  // open: gt, lt
  Comparator #(.mode("unsigned"), .width(3)) comparator_3 (
    .a(openALURS[5:3]), .b(3'b000), .eq(comparator_3_eq));  // open: gt, lt
  Comparator #(.mode("unsigned"), .width(3)) comparator_4 (
    .a(openLDSTRS[2:0]), .b(3'b000), .eq(comparator_4_eq));  // open: gt, lt
  Comparator #(.mode("unsigned"), .width(3)) comparator_5 (
    .a(openLDSTRS[5:3]), .b(3'b000), .eq(comparator_5_eq));  // open: gt, lt
  not not_1 (openALUstations1, comparator_2_eq);
  not not_2 (openALUstations2, comparator_3_eq);
  not not_3 (openLDSTstations1, comparator_4_eq);
  not not_4 (openLDSTstations2, comparator_5_eq);
  not not_5 (not_5_out, ICacheIns1[7]);
  not not_6 (not_6_out, ICacheIns1[6]);
  not not_7 (not_7_out, ICacheIns1[4]);
  not not_8 (not_8_out, ICacheIns1[5]);
  not not_9 (not_9_out, ICacheIns1[3]);
  not not_10 (not_10_out, ICacheIns1[2]);
  not not_11 (not_11_out, ICacheIns1[1]);
  not not_12 (not_12_out, ICacheIns1[0]);
  and and_1 (nop1, not_5_out, not_6_out, not_8_out, not_7_out, not_9_out, ICacheIns1[2], ICacheIns1[1], not_12_out);
  and and_2 (halt1, ICacheIns1[7], ICacheIns1[6], ICacheIns1[5], ICacheIns1[4], not_9_out, ICacheIns1[2], ICacheIns1[1], not_12_out);
  and and_3 (jmp1, not_12_out, not_11_out);
  and and_4 (ldi1, ICacheIns1[3], ICacheIns1[2], ICacheIns1[1], not_12_out);
  and and_5 (mv1, not_9_out, ICacheIns1[2], ICacheIns1[1], not_12_out);
  and and_6 (ld1, ICacheIns1[3], ICacheIns1[2], ICacheIns1[1], ICacheIns1[0]);
  and and_7 (add1, not_9_out, not_10_out, ICacheIns1[1], not_12_out);
  and and_8 (sub1, not_9_out, not_10_out, ICacheIns1[1], ICacheIns1[0]);
  and and_9 (st1, ICacheIns1[3], not_10_out, ICacheIns1[1], ICacheIns1[0]);
  and and_10 (jmpn1, not_11_out, ICacheIns1[0]);
  or or_1 (or_1_out, ldi1, mv1, ld1, add1, sub1);
  Multiplexer #(.width(45)) multiplexer_1 (
    .in0({newRS1, QkOut1, QjOut1, VkOut1, VjOut1, ICacheIns1[3:0]}), .in1({45{1'b0}}), .out(openRSIns1),
    .sel(stall1));
  not not_13 (not_13_out, nop1);
  or or_2 (needsRs1, mv1, ld1, add1, sub1, st1);
  or or_3 (needsRd1, sub1, add1, st1);
  and and_11 (writesRd1, or_1_out, not_13_out);
  or or_4 (branchIns1, jmpn1, jmp1);
  not not_14 (not_14_out, openLDSTstations1);
  or or_5 (ldstIns1, ld1, st1);
  not not_15 (not_15_out, openALUstations1);
  or or_6 (aluIns1, halt1, ldi1, mv1, add1, sub1);
  and and_12 (and_12_out, not_14_out, ldstIns1);
  and and_13 (and_13_out, jumpBusy, branchIns1);
  and and_14 (and_14_out, not_15_out, aluIns1);
  and and_15 (and_15_out, recentReady, jmpn1);
  Comparator #(.width(3)) comparator_6 (.a(regStatRS[2:0]), .b(3'b000), .eq(comparator_6_eq));  // open: gt, lt
  or or_7 (nostations1, and_13_out, and_12_out, and_14_out);
  Multiplexer #(.width(16)) multiplexer_2 (.in0(multiplexer_3_out), .in1({16{1'b1}}), .out(VjOut1), .sel(jmp1));
  Multiplexer #(.width(16)) multiplexer_3 (
    .in0(multiplexer_4_out), .in1(recentVal), .out(multiplexer_3_out), .sel(and_15_out));
  Multiplexer #(.width(16)) multiplexer_4 (
    .in0(multiplexer_5_out), .in1({{14{1'b0}}, ICacheIns1[5:4]}), .out(multiplexer_4_out), .sel(ldi1));
  Multiplexer #(.width(16)) multiplexer_5 (
    .in0({16{1'b0}}), .in1(regReadRes[15:0]), .out(multiplexer_5_out), .sel(comparator_6_eq));
  not not_16 (not_16_out, comparator_6_eq);
  not not_17 (not_17_out, nostations1);
  not not_18 (not_18_out, stall1);
  and and_16 (and_16_out, not_16_out, needsRs1);
  and and_17 (and_17_out, writesRd1, not_17_out, not_18_out);
  Multiplexer #(.width(3)) multiplexer_6 (.in0(multiplexer_7_out), .in1(recentRS), .out(QjOut1), .sel(jmpn1));
  Multiplexer #(.width(3)) multiplexer_7 (
    .in0(3'b000), .in1(regStatRS[2:0]), .out(multiplexer_7_out), .sel(and_16_out));
  Multiplexer #(.width(3)) multiplexer_8 (.in0(3'b000), .in1(newRS1), .out(newIns1RS), .sel(and_17_out));
  or or_8 (or_8_out, nostations1, jumpBusy, nop1);
  Multiplexer #(.width(3)) multiplexer_9 (.in0(multiplexer_10_out), .in1(3'b000), .out(newRS1), .sel(or_8_out));
  Multiplexer #(.width(3)) multiplexer_10 (
    .in0(multiplexer_11_out), .in1(jumpRS), .out(multiplexer_10_out), .sel(branchIns1));
  Multiplexer #(.width(3)) multiplexer_11 (
    .in0(multiplexer_12_out), .in1(openALURS[2:0]), .out(multiplexer_11_out), .sel(aluIns1));
  Multiplexer #(.width(3)) multiplexer_12 (
    .in0(3'b000), .in1(openLDSTRS[2:0]), .out(multiplexer_12_out), .sel(ldstIns1));
  or or_9 (or_9_out, jmp1, jmpn1);
  Comparator #(.width(3)) comparator_7 (.a(regStatRS[5:3]), .b(3'b000), .eq(comparator_7_eq));  // open: gt, lt
  not not_19 (not_19_out, comparator_7_eq);
  Multiplexer #(.width(16)) multiplexer_13 (
    .in0(multiplexer_14_out), .in1({{10{1'b0}}, ICacheIns1[7:2]}), .out(VkOut1), .sel(or_9_out));
  Multiplexer #(.width(16)) multiplexer_14 (
    .in0({16{1'b0}}), .in1(regReadRes[31:16]), .out(multiplexer_14_out), .sel(comparator_7_eq));
  and and_18 (and_18_out, not_19_out, needsRd1);
  or or_10 (or_10_out, jumpBusy, nostations1);
  not not_20 (not_20_out, nop1);
  Multiplexer #(.width(3)) multiplexer_15 (.in0(3'b000), .in1(regStatRS[5:3]), .out(QkOut1), .sel(and_18_out));
  and and_19 (stall1, or_10_out, not_20_out);
  not not_21 (not_21_out, ICacheIns2[7]);
  not not_22 (not_22_out, ICacheIns2[6]);
  not not_23 (not_23_out, ICacheIns2[5]);
  not not_24 (not_24_out, ICacheIns2[4]);
  not not_25 (not_25_out, ICacheIns2[3]);
  not not_26 (not_26_out, ICacheIns2[2]);
  not not_27 (not_27_out, ICacheIns2[1]);
  not not_28 (not_28_out, ICacheIns2[0]);
  and and_20 (nop2, not_21_out, not_22_out, not_23_out, not_24_out, not_25_out, ICacheIns2[2], ICacheIns2[1], not_28_out);
  and and_21 (halt2, ICacheIns2[7], ICacheIns2[6], ICacheIns2[5], ICacheIns2[4], not_25_out, ICacheIns2[2], ICacheIns2[1], not_28_out);
  and and_22 (jmp2, not_28_out, not_27_out);
  and and_23 (ldi2, ICacheIns2[3], ICacheIns2[2], ICacheIns2[1], not_28_out);
  and and_24 (mv2, not_25_out, ICacheIns2[2], ICacheIns2[1], not_28_out);
  and and_25 (ld2, ICacheIns2[3], ICacheIns2[2], ICacheIns2[1], ICacheIns2[0]);
  and and_26 (add2, not_25_out, not_26_out, ICacheIns2[1], not_28_out);
  and and_27 (sub2, not_25_out, not_26_out, ICacheIns2[1], ICacheIns2[0]);
  and and_28 (st2, ICacheIns2[3], not_26_out, ICacheIns2[1], ICacheIns2[0]);
  and and_29 (jmpn2, not_27_out, ICacheIns2[0]);
  or or_11 (or_11_out, stall2, stall1);
  Multiplexer #(.width(45)) multiplexer_16 (
    .in0({newRS2, QkOut2, QjOut2, VkOut2, VjOut2, ICacheIns2[3:0]}), .in1({45{1'b0}}), .out(openRSIns2),
    .sel(or_11_out));
  or or_12 (needsRs2, mv2, ld2, add2, sub2, st2);
  or or_13 (or_13_out, ldi2, mv2, ld2, add2, sub2);
  or or_14 (needsRd2, sub2, add2, st2);
  not not_29 (not_29_out, nop2);
  and and_30 (writesRd2, or_13_out, not_29_out);
  Comparator #(.width(2)) comparator_8 (
    .a(ICacheIns1[7:6]), .b(ICacheIns2[5:4]), .eq(comparator_8_eq));  // open: gt, lt
  and and_31 (and_31_out, openLDSTstations1, not_30_out);
  not not_30 (not_30_out, ldstIns1);
  and and_32 (and_32_out, openALUstations1, not_31_out);
  not not_31 (not_31_out, aluIns1);
  and and_33 (and_33_out, writesRd1, comparator_8_eq);
  or or_15 (or_15_out, and_31_out, openLDSTstations2);
  or or_16 (or_16_out, and_32_out, openALUstations2);
  Multiplexer #(.width(3)) multiplexer_17 (
    .in0(regStatRS[8:6]), .in1(newRS1), .out(multiplexer_17_out), .sel(and_33_out));
  or or_17 (or_17_out, branchIns1, jumpBusy);
  or or_18 (branchIns2, jmpn2, jmp2);
  not not_32 (not_32_out, or_15_out);
  or or_19 (ldstIns2, ld2, st2);
  not not_33 (not_33_out, or_16_out);
  or or_20 (aluIns2, halt2, ldi2, mv2, add2, sub2);
  not not_34 (not_34_out, writesRd1);
  Comparator #(.width(3)) comparator_9 (.a(multiplexer_17_out), .b(3'b000), .eq(comparator_9_eq));  // open: gt, lt
  and and_34 (and_34_out, or_17_out, branchIns2);
  and and_35 (and_35_out, not_32_out, ldstIns2);
  and and_36 (and_36_out, recentReady, not_34_out, jmpn2);
  not not_35 (not_35_out, nostations2);
  not not_36 (not_36_out, stall2);
  not not_37 (not_37_out, stall1);
  and and_37 (and_37_out, not_33_out, aluIns2);
  Multiplexer #(.width(16)) multiplexer_18 (.in0(multiplexer_19_out), .in1({16{1'b1}}), .out(VjOut2), .sel(jmp2));
  Multiplexer #(.width(16)) multiplexer_19 (
    .in0(multiplexer_20_out), .in1(recentVal), .out(multiplexer_19_out), .sel(and_36_out));
  Multiplexer #(.width(16)) multiplexer_20 (
    .in0(multiplexer_21_out), .in1({{14{1'b0}}, ICacheIns2[5:4]}), .out(multiplexer_20_out), .sel(ldi2));
  Multiplexer #(.width(16)) multiplexer_21 (
    .in0({16{1'b0}}), .in1(regReadRes[47:32]), .out(multiplexer_21_out), .sel(comparator_9_eq));
  and and_38 (and_38_out, writesRd2, not_35_out, not_36_out, not_37_out);
  or or_21 (nostations2, and_34_out, and_35_out, and_37_out);
  Multiplexer #(.width(3)) multiplexer_22 (.in0(recentRS), .in1(newRS1), .out(multiplexer_22_out), .sel(writesRd1));
  not not_38 (not_38_out, comparator_9_eq);
  and and_39 (and_39_out, not_38_out, needsRs2);
  Multiplexer #(.width(3)) multiplexer_23 (.in0(3'b000), .in1(newRS2), .out(newIns2RS), .sel(and_38_out));
  Multiplexer #(.width(3)) multiplexer_24 (
    .in0(multiplexer_25_out), .in1(multiplexer_22_out), .out(QjOut2), .sel(jmpn2));
  Multiplexer #(.width(3)) multiplexer_25 (
    .in0(3'b000), .in1(multiplexer_17_out), .out(multiplexer_25_out), .sel(and_39_out));
  not not_39 (not_39_out, aluIns1);
  not not_40 (not_40_out, ldstIns1);
  Comparator #(.width(2)) comparator_10 (
    .a(ICacheIns1[7:6]), .b(ICacheIns2[7:6]), .eq(comparator_10_eq));  // open: gt, lt
  and and_40 (and_40_out, not_39_out, aluIns2);
  and and_41 (and_41_out, not_40_out, ldstIns2);
  and and_42 (and_42_out, writesRd1, comparator_10_eq);
  or or_22 (or_22_out, nostations2, jumpBusy, nop2);
  Multiplexer #(.width(3)) multiplexer_26 (
    .in0(regStatRS[11:9]), .in1(newRS1), .out(multiplexer_26_out), .sel(and_42_out));
  Multiplexer #(.width(3)) multiplexer_27 (.in0(multiplexer_28_out), .in1(3'b000), .out(newRS2), .sel(or_22_out));
  Multiplexer #(.width(3)) multiplexer_28 (
    .in0(multiplexer_29_out), .in1(openALURS[2:0]), .out(multiplexer_28_out), .sel(and_40_out));
  Multiplexer #(.width(3)) multiplexer_29 (
    .in0(multiplexer_30_out), .in1(openLDSTRS[2:0]), .out(multiplexer_29_out), .sel(and_41_out));
  Multiplexer #(.width(3)) multiplexer_30 (
    .in0(multiplexer_31_out), .in1(jumpRS), .out(multiplexer_30_out), .sel(branchIns2));
  Multiplexer #(.width(3)) multiplexer_31 (
    .in0(multiplexer_32_out), .in1(openALURS[5:3]), .out(multiplexer_31_out), .sel(aluIns2));
  Multiplexer #(.width(3)) multiplexer_32 (
    .in0(3'b000), .in1(openLDSTRS[5:3]), .out(multiplexer_32_out), .sel(ldstIns2));
  or or_23 (or_23_out, jmp2, jmpn2);
  Comparator #(.width(3)) comparator_11 (.a(multiplexer_26_out), .b(3'b000), .eq(comparator_11_eq));  // open: gt, lt
  or or_24 (or_24_out, jumpBusy, nostations2);
  not not_41 (not_41_out, nop2);
  not not_42 (not_42_out, comparator_11_eq);
  and and_43 (and_43_out, not_42_out, needsRd2);
  and and_44 (stall2, or_24_out, not_41_out);
  Multiplexer #(.width(16)) multiplexer_33 (
    .in0(multiplexer_34_out), .in1({{10{1'b0}}, ICacheIns2[7:2]}), .out(VkOut2), .sel(or_23_out));
  Multiplexer #(.width(16)) multiplexer_34 (
    .in0({16{1'b0}}), .in1(regReadRes[63:48]), .out(multiplexer_34_out), .sel(comparator_11_eq));
  Multiplexer #(.width(3)) multiplexer_35 (.in0(3'b000), .in1(multiplexer_26_out), .out(QkOut2), .sel(and_43_out));

  assign newIns1Rd = ICacheIns1[7:6];
  assign newIns2Rd = ICacheIns2[7:6];
  assign regReadR = {ICacheIns2[7:4], ICacheIns1[7:4]};
  assign regStatR = {ICacheIns2[7:4], ICacheIns1[7:4]};

  // Other names for the same wires on the sheet: Iop1[3:0] = ICacheIns1[3:0]; jumpAddr1[5:0] = ICacheIns1[7:2];
  //   IRs1[1:0] = ICacheIns1[5:4]; RegRead1R[1:0] = ICacheIns1[5:4]; RegStat1R[1:0] = ICacheIns1[5:4];
  //   IRd1[1:0] = ICacheIns1[7:6]; RegRead2R[1:0] = ICacheIns1[7:6]; RegStat2R[1:0] = ICacheIns1[7:6];
  //   Iop2[3:0] = ICacheIns2[3:0]; jumpAddr2[5:0] = ICacheIns2[7:2]; IRs2[1:0] = ICacheIns2[5:4];
  //   RegRead3R[1:0] = ICacheIns2[5:4]; RegStat3R[1:0] = ICacheIns2[5:4]; IRd2[1:0] = ICacheIns2[7:6];
  //   RegRead4R[1:0] = ICacheIns2[7:6]; RegStat4R[1:0] = ICacheIns2[7:6]; openALURS1[2:0] = openALURS[2:0];
  //   openALURS2[2:0] = openALURS[5:3]; openLDSTRS1[2:0] = openLDSTRS[2:0]; openLDSTRS2[2:0] = openLDSTRS[5:3];
  //   RegRead1res[15:0] = regReadRes[15:0]; RegRead2res[15:0] = regReadRes[31:16];
  //   RegRead3res[15:0] = regReadRes[47:32]; RegRead4res[15:0] = regReadRes[63:48]; RegStat1RS[2:0] = regStatRS[2:0];
  //   RegStat2RS[2:0] = regStatRS[5:3]; RegStat3RS[2:0] = regStatRS[8:6]; RegStat4RS[2:0] = regStatRS[11:9]

  // Notes on the sheet:
  //   Register Interface
  //   To Stations
  //   no dependencies
  //   need just rs
  //   need rs and rd
  //   needs most recent
  //   jmp conditional must be negative
  //   Instruction 1
  //   J / Rs / most recent (jump cond)
  //   no stations
  //   for instruction
  //   Vj
  //   Update stats
  //   RS#
  //   Qj
  //   Stall
  //   k / Rd / jump addr
  //   stop two if 1 is branch instructions
  //   Vk
  //   make stall fully block ins2
  //   Qk
  //   To Stations
  //   no dependencies
  //   need just rs
  //   need rs and rd
  //   needs most recent
  //   jmp conditional must be negative
  //   J / Rs / most recent (jump cond)
  //   Update stats
  //   Instruction 2
  //   Vj
  //   RS#
  //   no stations
  //   for instruction
  //   Qj
  //   Stall
  //   k / Rd / jump addr
  //   Vk
  //   Qk
endmodule

module PC (
  input  clk,
  input  rst,
  input  stall2,
  input  stall1,
  input  [31:0] CDBdatas,
  input  [2:0] jumpRS,
  input  [5:0] CDBRSs,
  input  [15:0] ICacheData,
  output [4:0] ICacheAddr,
  output [7:0] ins2,
  output [7:0] ins1
);

  wire and_1_out, comparator_1_eq, odd, or_1_out;
  wire [5:0] adder_1_out, multiplexer_1_out, multiplexer_2_out, register_1_q;

  or or_1 (or_1_out, stall2, odd);
  Multiplexer #(.width(6)) multiplexer_1 (.in0(6'b000010), .in1(6'b000001), .out(multiplexer_1_out), .sel(or_1_out));
  Multiplexer #(.width(6)) multiplexer_2 (
    .in0(multiplexer_1_out), .in1({6{1'b0}}), .out(multiplexer_2_out), .sel(stall1));
  Adder #(.width(6)) adder_1 (.a(multiplexer_2_out), .b({ICacheAddr, odd}), .out(adder_1_out));  // open: cin, cout
  Multiplexer #(.width(8)) multiplexer_3 (.in0(ICacheData[7:0]), .in1(8'h6), .out(ins2), .sel(odd));
  Multiplexer #(.width(8)) multiplexer_4 (.in0(ICacheData[15:8]), .in1(ICacheData[7:0]), .out(ins1), .sel(odd));
  Comparator #(.width(3)) comparator_1 (.a(jumpRS), .b(CDBRSs[2:0]), .eq(comparator_1_eq));  // open: gt, lt
  Register #(.width(6)) register_1 (.D(adder_1_out), .en(1'b1), .clk(clk), .Q(register_1_q), .clr(rst));
  and and_1 (and_1_out, CDBdatas[15], comparator_1_eq);
  Multiplexer #(.width(6)) multiplexer_5 (
    .in0(register_1_q), .in1(CDBdatas[5:0]), .out({ICacheAddr, odd}), .sel(and_1_out));

  // Notes on the sheet:
  //   nop
  //   branch?
endmodule

module CDBManager (
  input  [2:0] branchRS,
  input  [15:0] branchData,
  input  branchReady,
  input  [2:0] ldstRS,
  input  ldstDone,
  input  [15:0] ldstData,
  input  ldstStore,
  input  [2:0] alu1RS,
  input  alu1done,
  input  [15:0] alu1data,
  input  [2:0] alu2RS,
  input  alu2done,
  input  [15:0] alu2data,
  input  [2:0] alu3RS,
  input  alu3done,
  input  [15:0] alu3data,
  output [5:0] RSs,
  output [31:0] datas
);

  wire and_1_out, and_2_out, and_3_out, and_4_out, and_5_out, not_1_out, or_1_out, or_2_out, or_3_out;
  wire [2:0] multiplexer_2_out, multiplexer_3_out, multiplexer_4_out, multiplexer_5_out, multiplexer_7_out,
       multiplexer_8_out, multiplexer_9_out;
  wire [15:0] multiplexer_11_out, multiplexer_12_out, multiplexer_13_out, multiplexer_14_out,
       multiplexer_16_out, multiplexer_17_out, multiplexer_18_out;

  not not_1 (not_1_out, ldstStore);
  and and_1 (and_1_out, ldstDone, not_1_out);
  Multiplexer #(.width(3)) multiplexer_1 (.in0(multiplexer_2_out), .in1(branchRS), .out(RSs[2:0]), .sel(branchReady));
  Multiplexer #(.width(3)) multiplexer_2 (
    .in0(multiplexer_3_out), .in1(ldstRS), .out(multiplexer_2_out), .sel(and_1_out));
  Multiplexer #(.width(3)) multiplexer_3 (
    .in0(multiplexer_4_out), .in1(alu1RS), .out(multiplexer_3_out), .sel(alu1done));
  Multiplexer #(.width(3)) multiplexer_4 (
    .in0(multiplexer_5_out), .in1(alu2RS), .out(multiplexer_4_out), .sel(alu2done));
  Multiplexer #(.width(3)) multiplexer_5 (.in0(3'b000), .in1(alu3RS), .out(multiplexer_5_out), .sel(alu3done));
  or or_1 (or_1_out, branchReady, branchReady);
  or or_2 (or_2_out, or_1_out, alu1done);
  or or_3 (or_3_out, or_2_out, alu2done);
  Multiplexer #(.width(3)) multiplexer_6 (.in0(multiplexer_7_out), .in1(ldstRS), .out(RSs[5:3]), .sel(and_2_out));
  and and_2 (and_2_out, branchReady, and_1_out);
  Multiplexer #(.width(3)) multiplexer_7 (
    .in0(multiplexer_8_out), .in1(alu1RS), .out(multiplexer_7_out), .sel(and_3_out));
  and and_3 (and_3_out, or_1_out, alu1done);
  Multiplexer #(.width(3)) multiplexer_8 (
    .in0(multiplexer_9_out), .in1(alu2RS), .out(multiplexer_8_out), .sel(and_4_out));
  and and_4 (and_4_out, or_2_out, alu2done);
  Multiplexer #(.width(3)) multiplexer_9 (.in0(3'b000), .in1(alu3RS), .out(multiplexer_9_out), .sel(and_5_out));
  and and_5 (and_5_out, or_3_out, alu3done);
  Multiplexer #(.width(16)) multiplexer_10 (
    .in0(multiplexer_11_out), .in1(branchData), .out(datas[15:0]), .sel(branchReady));
  Multiplexer #(.width(16)) multiplexer_11 (
    .in0(multiplexer_12_out), .in1(ldstData), .out(multiplexer_11_out), .sel(and_1_out));
  Multiplexer #(.width(16)) multiplexer_12 (
    .in0(multiplexer_13_out), .in1(alu1data), .out(multiplexer_12_out), .sel(alu1done));
  Multiplexer #(.width(16)) multiplexer_13 (
    .in0(multiplexer_14_out), .in1(alu2data), .out(multiplexer_13_out), .sel(alu2done));
  Multiplexer #(.width(16)) multiplexer_14 (.in0({16{1'b0}}), .in1(alu3data), .out(multiplexer_14_out), .sel(alu3done));
  Multiplexer #(.width(16)) multiplexer_15 (
    .in0(multiplexer_16_out), .in1(ldstData), .out(datas[31:16]), .sel(and_2_out));
  Multiplexer #(.width(16)) multiplexer_16 (
    .in0(multiplexer_17_out), .in1(alu1data), .out(multiplexer_16_out), .sel(and_3_out));
  Multiplexer #(.width(16)) multiplexer_17 (
    .in0(multiplexer_18_out), .in1(alu2data), .out(multiplexer_17_out), .sel(and_4_out));
  Multiplexer #(.width(16)) multiplexer_18 (
    .in0({16{1'b0}}), .in1(alu3data), .out(multiplexer_18_out), .sel(and_5_out));

  // Notes on the sheet:
  //   done1rs
  //   something above done
  //   done2rs
  //   branches always in 2-0
  //   done1data
  //   done2data
endmodule

module JumpCompare (
  input  [2:0] RS,
  input  ready,
  input  [5:0] address,
  input  [15:0] negCond,
  output [2:0] RSo,
  output readyO,
  output [15:0] data
);

  Comparator #(.width(16)) comparator_1 (.a(negCond), .b({16{1'b0}}), .lt(data[15]));  // open: gt, eq

  assign data[14:0] = {{9{1'b0}}, address};
  assign readyO = ready;
  assign RSo = RS;

  // Notes on the sheet:
  //   CBD format
endmodule
